// Logisim project key.circ as structural Verilog: 1 circuit, main circuit main
module main (
  input  [3:0] in_1,
  input  [3:0] in_2,
  input  in_3,
  output [7:0] N,
  output [7:0] E,
  output [7:0] out_6,
  output [7:0] D
);

  wire button_1_out;
  wire [7:0] bit_extender_1_out, bit_extender_2_out, multiplier_2_out, multiplier_3_out, subtractor_1_out,
       subtractor_2_out;

  assign bit_extender_1_out = {{4{1'b0}}, in_1};  // Bit_Extender bit_extender_1
  assign bit_extender_2_out = {{4{1'b0}}, in_2};  // Bit_Extender bit_extender_2
  Multiplier multiplier_1 (.a(bit_extender_1_out), .b(bit_extender_2_out), .out(N));  // open: cin, cout
  Subtractor subtractor_1 (.a(bit_extender_1_out), .b(8'h1), .out(subtractor_1_out));  // open: bin, bout
  Subtractor subtractor_2 (.a(bit_extender_2_out), .b(8'h1), .out(subtractor_2_out));  // open: bin, bout
  Multiplier multiplier_2 (.a(subtractor_1_out), .b(subtractor_2_out), .out(multiplier_2_out));  // open: cin, cout
  Button button_1 (.out(button_1_out));
  Multiplier multiplier_3 (.a(multiplier_2_out), .b(8'h2), .out(multiplier_3_out));  // open: cin, cout
  Counter #(.trigger("falling")) counter_1 (.Q(E), .clk(button_1_out), .clr(in_3));  // open: load, D, count, carry
  Adder adder_1 (.a(multiplier_3_out), .b({8{1'b1}}), .out(D));  // open: cin, cout
  Divider divider_1 (.a(multiplier_2_out), .b(E), .rem(out_6));  // open: out, upper
endmodule
